// Logisim project t1_ula_logisim.circ as structural Verilog
module half_adder (
  input  A,
  input  B,
  output SUM,
  output CARRY
);

  xor xor_1 (SUM, A, B);
  and and_1 (CARRY, A, B);
endmodule

module full_adder (
  input  A,
  input  B,
  input  CIN,
  output COUT,
  output SUM
);

  wire half_adder_0_carry, half_adder_0_sum, half_adder_1_carry;

  half_adder half_adder_0 (.A(A), .B(B), .SUM(half_adder_0_sum), .CARRY(half_adder_0_carry));
  half_adder half_adder_1 (.A(half_adder_0_sum), .B(CIN), .SUM(SUM), .CARRY(half_adder_1_carry));
  or or_1 (COUT, half_adder_0_carry, half_adder_1_carry);
endmodule

module adder8 (
  input  CIN,
  input  [7:0] A,
  input  [7:0] B,
  output [7:0] SUM,
  output COUT
);

  wire full_adder_1_cout, full_adder_2_cout, full_adder_3_cout, full_adder_4_cout, full_adder_5_cout,
       full_adder_6_cout, full_adder_7_cout;

  full_adder full_adder_1 (.A(A[0]), .B(B[0]), .CIN(CIN), .COUT(full_adder_1_cout), .SUM(SUM[0]));
  full_adder full_adder_2 (.A(A[1]), .B(B[1]), .CIN(full_adder_1_cout), .COUT(full_adder_2_cout), .SUM(SUM[1]));
  full_adder full_adder_3 (.A(A[2]), .B(B[2]), .CIN(full_adder_2_cout), .COUT(full_adder_3_cout), .SUM(SUM[2]));
  full_adder full_adder_4 (.A(A[3]), .B(B[3]), .CIN(full_adder_3_cout), .COUT(full_adder_4_cout), .SUM(SUM[3]));
  full_adder full_adder_5 (.A(A[4]), .B(B[4]), .CIN(full_adder_4_cout), .COUT(full_adder_5_cout), .SUM(SUM[4]));
  full_adder full_adder_6 (.A(A[5]), .B(B[5]), .CIN(full_adder_5_cout), .COUT(full_adder_6_cout), .SUM(SUM[5]));
  full_adder full_adder_7 (.A(A[6]), .B(B[6]), .CIN(full_adder_6_cout), .COUT(full_adder_7_cout), .SUM(SUM[6]));
  full_adder full_adder_8 (.A(A[7]), .B(B[7]), .CIN(full_adder_7_cout), .COUT(COUT), .SUM(SUM[7]));
endmodule

module ula8 (
  input  [2:0] OP,
  input  [7:0] A,
  input  [7:0] B,
  output [15:0] out_4
);

  wire comparator_1_eq, comparator_2_eq, not_1_out;
  wire [7:0] adder8_1_sum, ANDGATE_out, bit_extender_1_out, bit_extender_7_out, NOTGATE_out, ORGATE_out,
       xor_1_out, XORGATE_out;
  wire [8:8] adder8_1_cout;
  wire [15:0] bit_extender_2_out, bit_extender_3_out, bit_extender_4_out, bit_extender_5_out,
       bit_extender_6_out, multiplier8v2_1_product;

  assign xor_1_out = B ^ bit_extender_7_out;  // XOR_Gate xor_1, 8 bits wide
  assign ANDGATE_out = A & B;  // AND_Gate ANDGATE, 8 bits wide
  assign ORGATE_out = A | B;  // OR_Gate ORGATE, 8 bits wide
  assign NOTGATE_out = ~A;  // NOT_Gate NOTGATE, 8 bits wide
  assign XORGATE_out = A ^ B;  // XOR_Gate XORGATE, 8 bits wide
  multiplier8v2 multiplier8v2_1 (.A(A), .B(B), .PRODUCT(multiplier8v2_1_product));
  Comparator comparator_1 (.a(A), .b(B), .eq(comparator_1_eq));  // open: gt, lt
  adder8 adder8_1 (.CIN(comparator_2_eq), .A(A), .B(xor_1_out), .SUM(adder8_1_sum), .COUT(adder8_1_cout[8]));
  not not_1 (not_1_out, adder8_1_cout[8]);
  assign bit_extender_1_out = {{7{not_1_out}}, not_1_out};  // Bit_Extender bit_extender_1
  assign bit_extender_2_out = {{8{1'b0}}, ANDGATE_out};  // Bit_Extender bit_extender_2
  assign bit_extender_3_out = {{8{1'b0}}, ORGATE_out};  // Bit_Extender bit_extender_3
  assign bit_extender_4_out = {{8{1'b0}}, NOTGATE_out};  // Bit_Extender bit_extender_4
  assign bit_extender_5_out = {{8{1'b0}}, XORGATE_out};  // Bit_Extender bit_extender_5
  assign bit_extender_6_out = {{15{1'b0}}, comparator_1_eq};  // Bit_Extender bit_extender_6
  Comparator #(.width(3)) comparator_2 (.a(OP), .b(3'b001), .eq(comparator_2_eq));  // open: gt, lt
  assign bit_extender_7_out = {{7{comparator_2_eq}}, comparator_2_eq};  // Bit_Extender bit_extender_7
  Multiplexer #(.select(3), .width(16)) multiplexer_1 (
    .in0({{7{1'b0}}, adder8_1_cout[8], adder8_1_sum}), .in1({bit_extender_1_out, adder8_1_sum}),
    .in2(multiplier8v2_1_product), .in3(bit_extender_6_out), .in4(bit_extender_2_out),
    .in5(bit_extender_3_out), .in6(bit_extender_4_out), .in7(bit_extender_5_out), .out(out_4), .sel(OP));
endmodule

module multiplier8v2 (
  input  [7:0] A,
  input  [7:0] B,
  output [15:0] PRODUCT
);

  wire and_1_out, and_2_out, and_3_out, and_4_out, and_5_out, and_6_out, and_7_out, and_8_out, and_10_out,
       and_11_out, and_12_out, and_13_out, and_14_out, and_15_out, and_16_out, and_17_out, and_18_out,
       and_19_out, and_20_out, and_21_out, and_22_out, and_23_out, and_24_out, and_25_out, and_26_out,
       and_27_out, and_28_out, and_29_out, and_30_out, and_31_out, and_32_out, and_33_out, and_34_out,
       and_35_out, and_36_out, and_37_out, and_38_out, and_39_out, and_40_out, and_41_out, and_42_out,
       and_43_out, and_44_out, and_45_out, and_46_out, and_47_out, and_48_out, and_49_out, and_50_out,
       and_51_out, and_52_out, and_53_out, and_54_out, and_55_out, and_56_out, and_57_out, and_58_out,
       and_59_out, and_60_out, and_61_out, and_62_out, and_63_out, and_64_out, FA0_cout, FA0_sum, FA1_cout,
       FA1_sum, FA2_cout, FA2_sum, FA3_cout, FA3_sum, FA4_cout, FA4_sum, FA5_cout, FA5_sum, FA6_cout,
       FA6_sum, FA7_cout, FA7_sum, FA8_cout, FA8_sum, FA9_cout, FA9_sum, FA10_cout, FA10_sum, FA11_cout,
       FA11_sum, FA12_cout, FA12_sum, FA13_cout, FA13_sum, FA14_cout, FA14_sum, FA15_cout, FA15_sum,
       FA16_cout, FA16_sum, FA17_cout, FA17_sum, FA18_cout, FA18_sum, FA19_cout, FA19_sum, FA20_cout,
       FA20_sum, FA21_cout, FA21_sum, FA22_cout, FA22_sum, FA23_cout, FA23_sum, FA24_cout, FA24_sum,
       FA25_cout, FA25_sum, FA26_cout, FA26_sum, FA27_cout, FA27_sum, FA28_cout, FA28_sum, FA29_cout,
       FA29_sum, FA30_cout, FA30_sum, FA31_cout, FA31_sum, FA32_cout, FA32_sum, FA33_cout, FA33_sum,
       FA34_cout, FA34_sum, FA35_cout, FA35_sum, FA36_cout, FA36_sum, FA37_cout, FA37_sum, FA38_cout,
       FA38_sum, FA39_cout, FA39_sum, FA40_cout, FA40_sum, FA41_cout, FA41_sum, FA42_cout, FA43_cout,
       FA44_cout, FA45_cout, FA46_cout, FA47_cout, HA0_carry, HA1_carry, HA2_carry, HA3_carry, HA4_carry,
       HA5_carry, HA6_carry;

  and and_1 (and_1_out, A[0], B[2]);
  and and_2 (and_2_out, A[1], B[2]);
  and and_3 (and_3_out, A[2], B[2]);
  and and_4 (and_4_out, A[3], B[2]);
  and and_5 (and_5_out, A[4], B[2]);
  and and_6 (and_6_out, A[5], B[2]);
  and and_7 (and_7_out, A[6], B[2]);
  and and_8 (and_8_out, A[7], B[2]);
  and and_9 (PRODUCT[0], A[0], B[0]);
  and and_10 (and_10_out, A[1], B[0]);
  and and_11 (and_11_out, A[2], B[0]);
  and and_12 (and_12_out, A[3], B[0]);
  and and_13 (and_13_out, A[4], B[0]);
  and and_14 (and_14_out, A[5], B[0]);
  and and_15 (and_15_out, A[6], B[0]);
  and and_16 (and_16_out, A[7], B[0]);
  and and_17 (and_17_out, A[0], B[1]);
  and and_18 (and_18_out, A[1], B[1]);
  and and_19 (and_19_out, A[2], B[1]);
  and and_20 (and_20_out, A[3], B[1]);
  and and_21 (and_21_out, A[4], B[1]);
  and and_22 (and_22_out, A[5], B[1]);
  and and_23 (and_23_out, A[6], B[1]);
  and and_24 (and_24_out, A[7], B[1]);
  and and_25 (and_25_out, A[0], B[3]);
  and and_26 (and_26_out, A[1], B[3]);
  and and_27 (and_27_out, A[2], B[3]);
  and and_28 (and_28_out, A[3], B[3]);
  and and_29 (and_29_out, A[4], B[3]);
  and and_30 (and_30_out, A[5], B[3]);
  and and_31 (and_31_out, A[6], B[3]);
  and and_32 (and_32_out, A[7], B[3]);
  and and_33 (and_33_out, A[0], B[4]);
  and and_34 (and_34_out, A[1], B[4]);
  and and_35 (and_35_out, A[2], B[4]);
  and and_36 (and_36_out, A[3], B[4]);
  and and_37 (and_37_out, A[4], B[4]);
  and and_38 (and_38_out, A[5], B[4]);
  and and_39 (and_39_out, A[6], B[4]);
  and and_40 (and_40_out, A[7], B[4]);
  and and_41 (and_41_out, A[0], B[5]);
  and and_42 (and_42_out, A[1], B[5]);
  and and_43 (and_43_out, A[2], B[5]);
  and and_44 (and_44_out, A[3], B[5]);
  and and_45 (and_45_out, A[4], B[5]);
  and and_46 (and_46_out, A[5], B[5]);
  and and_47 (and_47_out, A[6], B[5]);
  and and_48 (and_48_out, A[7], B[5]);
  and and_49 (and_49_out, A[0], B[6]);
  and and_50 (and_50_out, A[1], B[6]);
  and and_51 (and_51_out, A[2], B[6]);
  and and_52 (and_52_out, A[3], B[6]);
  and and_53 (and_53_out, A[4], B[6]);
  and and_54 (and_54_out, A[5], B[6]);
  and and_55 (and_55_out, A[6], B[6]);
  and and_56 (and_56_out, A[7], B[6]);
  and and_57 (and_57_out, A[0], B[7]);
  and and_58 (and_58_out, A[1], B[7]);
  and and_59 (and_59_out, A[2], B[7]);
  and and_60 (and_60_out, A[3], B[7]);
  and and_61 (and_61_out, A[4], B[7]);
  and and_62 (and_62_out, A[5], B[7]);
  and and_63 (and_63_out, A[6], B[7]);
  and and_64 (and_64_out, A[7], B[7]);
  half_adder HA0 (.A(and_10_out), .B(and_17_out), .SUM(PRODUCT[1]), .CARRY(HA0_carry));
  full_adder FA0 (.A(and_11_out), .B(and_18_out), .CIN(HA0_carry), .COUT(FA0_cout), .SUM(FA0_sum));
  full_adder FA1 (.A(and_12_out), .B(and_19_out), .CIN(FA0_cout), .COUT(FA1_cout), .SUM(FA1_sum));
  full_adder FA2 (.A(and_13_out), .B(and_20_out), .CIN(FA1_cout), .COUT(FA2_cout), .SUM(FA2_sum));
  full_adder FA3 (.A(and_14_out), .B(and_21_out), .CIN(FA2_cout), .COUT(FA3_cout), .SUM(FA3_sum));
  full_adder FA4 (.A(and_15_out), .B(and_22_out), .CIN(FA3_cout), .COUT(FA4_cout), .SUM(FA4_sum));
  full_adder FA5 (.A(and_16_out), .B(and_23_out), .CIN(FA4_cout), .COUT(FA5_cout), .SUM(FA5_sum));
  full_adder FA6 (.A(1'b0), .B(and_24_out), .CIN(FA5_cout), .COUT(FA6_cout), .SUM(FA6_sum));
  half_adder HA1 (.A(FA0_sum), .B(and_1_out), .SUM(PRODUCT[2]), .CARRY(HA1_carry));
  full_adder FA7 (.A(FA1_sum), .B(and_2_out), .CIN(HA1_carry), .COUT(FA7_cout), .SUM(FA7_sum));
  full_adder FA8 (.A(FA2_sum), .B(and_3_out), .CIN(FA7_cout), .COUT(FA8_cout), .SUM(FA8_sum));
  full_adder FA9 (.A(FA3_sum), .B(and_4_out), .CIN(FA8_cout), .COUT(FA9_cout), .SUM(FA9_sum));
  full_adder FA10 (.A(FA4_sum), .B(and_5_out), .CIN(FA9_cout), .COUT(FA10_cout), .SUM(FA10_sum));
  full_adder FA11 (.A(FA5_sum), .B(and_6_out), .CIN(FA10_cout), .COUT(FA11_cout), .SUM(FA11_sum));
  full_adder FA12 (.A(FA6_sum), .B(and_7_out), .CIN(FA11_cout), .COUT(FA12_cout), .SUM(FA12_sum));
  full_adder FA13 (.A(FA6_cout), .B(and_8_out), .CIN(FA12_cout), .COUT(FA13_cout), .SUM(FA13_sum));
  half_adder HA2 (.A(FA7_sum), .B(and_25_out), .SUM(PRODUCT[3]), .CARRY(HA2_carry));
  full_adder FA14 (.A(FA8_sum), .B(and_26_out), .CIN(HA2_carry), .COUT(FA14_cout), .SUM(FA14_sum));
  full_adder FA15 (.A(FA9_sum), .B(and_27_out), .CIN(FA14_cout), .COUT(FA15_cout), .SUM(FA15_sum));
  full_adder FA16 (.A(FA10_sum), .B(and_28_out), .CIN(FA15_cout), .COUT(FA16_cout), .SUM(FA16_sum));
  full_adder FA17 (.A(FA11_sum), .B(and_29_out), .CIN(FA16_cout), .COUT(FA17_cout), .SUM(FA17_sum));
  full_adder FA18 (.A(FA12_sum), .B(and_30_out), .CIN(FA17_cout), .COUT(FA18_cout), .SUM(FA18_sum));
  full_adder FA19 (.A(FA13_sum), .B(and_31_out), .CIN(FA18_cout), .COUT(FA19_cout), .SUM(FA19_sum));
  full_adder FA20 (.A(FA13_cout), .B(and_32_out), .CIN(FA19_cout), .COUT(FA20_cout), .SUM(FA20_sum));
  half_adder HA3 (.A(FA14_sum), .B(and_33_out), .SUM(PRODUCT[4]), .CARRY(HA3_carry));
  full_adder FA21 (.A(FA15_sum), .B(and_34_out), .CIN(HA3_carry), .COUT(FA21_cout), .SUM(FA21_sum));
  full_adder FA22 (.A(FA16_sum), .B(and_35_out), .CIN(FA21_cout), .COUT(FA22_cout), .SUM(FA22_sum));
  full_adder FA23 (.A(FA17_sum), .B(and_36_out), .CIN(FA22_cout), .COUT(FA23_cout), .SUM(FA23_sum));
  full_adder FA24 (.A(FA18_sum), .B(and_37_out), .CIN(FA23_cout), .COUT(FA24_cout), .SUM(FA24_sum));
  full_adder FA25 (.A(FA19_sum), .B(and_38_out), .CIN(FA24_cout), .COUT(FA25_cout), .SUM(FA25_sum));
  full_adder FA26 (.A(FA20_sum), .B(and_39_out), .CIN(FA25_cout), .COUT(FA26_cout), .SUM(FA26_sum));
  full_adder FA27 (.A(FA20_cout), .B(and_40_out), .CIN(FA26_cout), .COUT(FA27_cout), .SUM(FA27_sum));
  half_adder HA4 (.A(FA21_sum), .B(and_41_out), .SUM(PRODUCT[5]), .CARRY(HA4_carry));
  full_adder FA28 (.A(FA22_sum), .B(and_42_out), .CIN(HA4_carry), .COUT(FA28_cout), .SUM(FA28_sum));
  full_adder FA29 (.A(FA23_sum), .B(and_43_out), .CIN(FA28_cout), .COUT(FA29_cout), .SUM(FA29_sum));
  full_adder FA30 (.A(FA24_sum), .B(and_44_out), .CIN(FA29_cout), .COUT(FA30_cout), .SUM(FA30_sum));
  full_adder FA31 (.A(FA25_sum), .B(and_45_out), .CIN(FA30_cout), .COUT(FA31_cout), .SUM(FA31_sum));
  full_adder FA32 (.A(FA26_sum), .B(and_46_out), .CIN(FA31_cout), .COUT(FA32_cout), .SUM(FA32_sum));
  full_adder FA33 (.A(FA27_sum), .B(and_47_out), .CIN(FA32_cout), .COUT(FA33_cout), .SUM(FA33_sum));
  full_adder FA34 (.A(FA27_cout), .B(and_48_out), .CIN(FA33_cout), .COUT(FA34_cout), .SUM(FA34_sum));
  half_adder HA5 (.A(FA28_sum), .B(and_49_out), .SUM(PRODUCT[6]), .CARRY(HA5_carry));
  full_adder FA35 (.A(FA29_sum), .B(and_50_out), .CIN(HA5_carry), .COUT(FA35_cout), .SUM(FA35_sum));
  full_adder FA36 (.A(FA30_sum), .B(and_51_out), .CIN(FA35_cout), .COUT(FA36_cout), .SUM(FA36_sum));
  full_adder FA37 (.A(FA31_sum), .B(and_52_out), .CIN(FA36_cout), .COUT(FA37_cout), .SUM(FA37_sum));
  full_adder FA38 (.A(FA32_sum), .B(and_53_out), .CIN(FA37_cout), .COUT(FA38_cout), .SUM(FA38_sum));
  full_adder FA39 (.A(FA33_sum), .B(and_54_out), .CIN(FA38_cout), .COUT(FA39_cout), .SUM(FA39_sum));
  full_adder FA40 (.A(FA34_sum), .B(and_55_out), .CIN(FA39_cout), .COUT(FA40_cout), .SUM(FA40_sum));
  full_adder FA41 (.A(FA34_cout), .B(and_56_out), .CIN(FA40_cout), .COUT(FA41_cout), .SUM(FA41_sum));
  half_adder HA6 (.A(FA35_sum), .B(and_57_out), .SUM(PRODUCT[7]), .CARRY(HA6_carry));
  full_adder FA42 (.A(FA36_sum), .B(and_58_out), .CIN(HA6_carry), .COUT(FA42_cout), .SUM(PRODUCT[8]));
  full_adder FA43 (.A(FA37_sum), .B(and_59_out), .CIN(FA42_cout), .COUT(FA43_cout), .SUM(PRODUCT[9]));
  full_adder FA44 (.A(FA38_sum), .B(and_60_out), .CIN(FA43_cout), .COUT(FA44_cout), .SUM(PRODUCT[10]));
  full_adder FA45 (.A(FA39_sum), .B(and_61_out), .CIN(FA44_cout), .COUT(FA45_cout), .SUM(PRODUCT[11]));
  full_adder FA46 (.A(FA40_sum), .B(and_62_out), .CIN(FA45_cout), .COUT(FA46_cout), .SUM(PRODUCT[12]));
  full_adder FA47 (.A(FA41_sum), .B(and_63_out), .CIN(FA46_cout), .COUT(FA47_cout), .SUM(PRODUCT[13]));
  full_adder FA48 (.A(FA41_cout), .B(and_64_out), .CIN(FA47_cout), .COUT(PRODUCT[15]), .SUM(PRODUCT[14]));
endmodule
